// Logisim project new_CPU_int.circ as structural Verilog: 8 circuits, main circuit main
module main (
  output [7:0] out_1,
  output [3:0] out_2
);

  wire Adress, ALU, ALUCarry, ALULogic, and_1_out, and_2_out, and_3_out, Clock, demultiplexer_1_out1, Digit,
       DoJump, FlagWrite, Halt, INT_io, IO_in, IO_out, Jump, not_1_out, or_1_out, or_2_out, RET, w, Write;
  wire [0:0] or_4_out;
  wire [1:0] myalu_1_sign, register_1_q;
  wire [3:0] A, A_in, ALUop, B, B_in, Data, ID, io_2digits_1_first, io_2digits_1_second, multiplexer_1_out,
       multiplexer_2_out, multiplexer_3_out, Operation, Outp, r0, r3, r4, r5, r6, r7, RAMDigit;

  and and_1 (and_1_out, Digit, Adress);
  and and_2 (and_2_out, ~IO_out, Write);  // AND_Gate
  or or_1 (or_1_out, and_2_out, IO_in);
  Demultiplexer #(.disabled("Z")) demultiplexer_1 (
    .out0(w), .out1(demultiplexer_1_out1), .in(or_1_out), .sel(or_2_out));
  or or_2 (or_2_out, IO_in, and_1_out);
  not not_1 (not_1_out, Digit);
  Registers registers_1 (
    .Data(Data), .A_in(A_in), .B_in(B_in), .w(w), .t(A_in), .r0(r0), .r1(out_1[7:4]), .r2(out_1[3:0]),
    .r3(r3), .r4(r4), .r5(r5), .r6(r6), .r7(r7), .A(A), .B(B));
  OperationDecoder operationdecoder_1 (
    .Operation(Operation), .Digit(Digit), .Jump(Jump), .ALULogic(ALULogic), .ALU(ALU), .ALUCarry(ALUCarry),
    .FlagWrite(FlagWrite), .Adress(Adress), .IO_out(IO_out), .Halt(Halt), .ALUop(ALUop), .INT_io(INT_io),
    .RET(RET));
  Multiplexer #(.disabled("Z"), .width(4)) multiplexer_1 (.in0(A), .in1(B), .out(multiplexer_1_out), .sel(not_1_out));
  Multiplexer #(.width(4)) multiplexer_2 (.in0(multiplexer_1_out), .in1(4'b1111), .out(multiplexer_2_out), .sel(IO_in));
  Hex_Digit_Display hex_digit_display_1 (.value(Data));  // open: dp
  RAM #(.addrWidth(4), .dataWidth(4), .enables("line")) ram_1 (
    .addr(multiplexer_2_out), .we(demultiplexer_1_out1), .clk(demultiplexer_1_out1), .din(Data),
    .dout(RAMDigit));
  Hex_Digit_Display hex_digit_display_2 (.value(A));  // open: dp
  Hex_Digit_Display hex_digit_display_3 (.value(Operation));  // open: dp
  Hex_Digit_Display hex_digit_display_4 (.value(B));  // open: dp
  Hex_Digit_Display hex_digit_display_5 (.value(A_in));  // open: dp
  MyALU myalu_1 (
    .Cin(ALUCarry), .Operation(ALUop), .A(A), .B(B), .M(ALULogic), .Outp(Outp), .AeqB(myalu_1_sign[1]),
    .Sign(myalu_1_sign[0]));
  Hex_Digit_Display hex_digit_display_6 (.value(Data));  // open: dp
  Hex_Digit_Display hex_digit_display_7 (.value(ID));  // open: dp
  Hex_Digit_Display hex_digit_display_8 (.value(B_in));  // open: dp
  Button button_1 (.out(out_2[0]));
  Button button_2 (.out(out_2[1]));
  Button button_3 (.out(out_2[2]));
  Button button_4 (.out(out_2[3]));
  and and_3 (and_3_out, FlagWrite, ~Clock);  // AND_Gate
  Clock clock_1 (.out(Clock));
  Register #(.width(2)) register_1 (.D(myalu_1_sign), .en(and_3_out), .clk(and_3_out), .Q(register_1_q));  // open: clr
  Hex_Digit_Display hex_digit_display_9 (.value(r0));  // open: dp
  Hex_Digit_Display hex_digit_display_10 (.value(out_1[7:4]));  // open: dp
  nor nor_1 (Write, Clock, Jump);
  Hex_Digit_Display hex_digit_display_11 (.value(r3));  // open: dp
  Hex_Digit_Display hex_digit_display_12 (.value(out_1[3:0]));  // open: dp
  or or_3 (IO_in, out_2[0], out_2[1], out_2[2], out_2[3]);
  TTY #(.cols(33), .rows(5)) tty_1 (.data(out_1[6:0]), .clk(out_1[7]), .we(1'b1));  // open: clr
  Hex_Digit_Display hex_digit_display_13 (.value(r4));  // open: dp
  Hex_Digit_Display hex_digit_display_14 (.value(r5));  // open: dp
  Hex_Digit_Display hex_digit_display_15 (.value(r6));  // open: dp
  Hex_Digit_Display hex_digit_display_16 (.value(r7));  // open: dp
  JumpHandler jumphandler_1 (
    .a(Operation[1]), .b(Operation[0]), .c(register_1_q[1]), .d(register_1_q[0]), .JumpOp(Jump),
    .DoJump(DoJump));
  PC pc_1 (
    .Clock(Clock), .DoJump(DoJump), .IO_in(IO_in), .RET(RET), .ClockWait(Halt), .INT_io(INT_io),
    .Operation(Operation), .A_in(A_in), .B_in(B_in));  // open: CA
  IO_2digits io_2digits_1 (
    .B(B), .A_in(A_in), .IO_out(IO_out), .Write(Write), .Adress(Adress), .first(io_2digits_1_first),
    .second(io_2digits_1_second));
  or or_4 (or_4_out[0], Digit, IO_out);
  Multiplexer #(.width(4)) multiplexer_3 (.in0(ID), .in1(Outp), .out(multiplexer_3_out), .sel(ALU));
  Hex_Digit_Display hex_digit_display_17 (.value(io_2digits_1_first));  // open: dp
  Hex_Digit_Display hex_digit_display_18 (.value(io_2digits_1_second));  // open: dp
  Multiplexer #(.select(2), .width(4)) multiplexer_4 (
    .in0(B), .in1(B_in), .in2(RAMDigit), .in3(B), .out(ID), .sel({Adress, or_4_out[0]}));
  Multiplexer #(.width(4)) multiplexer_5 (.in0(multiplexer_3_out), .in1(out_2), .out(Data), .sel(IO_in));

  // Other names for the same wires on the sheet: IO_data[3:0] = out_2; r2[3:0] = out_1[3:0]; ROut[7:0] = out_1;
  //   r1[3:0] = out_1[7:4]

  // Notes on the sheet:
  //   (Eq Bit)(Sign Bit)
endmodule

module MyALU (
  input  Cin,
  input  [3:0] Operation,
  input  [3:0] A,
  input  [3:0] B,
  input  M,
  output [3:0] Outp,
  output AeqB,
  output Sign
);

  wire n74181_1_p13, n74181_1_p14, n74181_1_p16, n74181_1_p18;

  // _74181 74181_1: pin names not known; wires that end beside it: B[0], A[1], A[0], B[1], Operation[3], A[2], Operation[2], B[2], Operation[1], A[3], Operation[0], B[3], n74181_1_p13, n74181_1_p14, M, n74181_1_p16, Outp[0], n74181_1_p18, Outp[1], AeqB, Outp[2], Outp[3]
  nor nor_1 (Sign, n74181_1_p14, AeqB);
  not not_1 (n74181_1_p13, Cin);

  // Notes on the sheet:
  //   Cout
  //   Pn
endmodule

module Registers (
  input  [3:0] Data,
  input  [3:0] A_in,
  input  [3:0] B_in,
  input  w,
  input  [3:0] t,
  output [3:0] r0,
  output [3:0] r1,
  output [3:0] r2,
  output [3:0] r3,
  output [3:0] r4,
  output [3:0] r5,
  output [3:0] r6,
  output [3:0] r7,
  output [3:0] A,
  output [3:0] B
);

  wire r0_w, r1_w, r2_w, r3_w, r4_w, r5_w, r6_w, r7_w;

  Register #(.width(4)) register_1 (.D(Data), .clk(r0_w), .Q(r0));  // open: en, clr
  Register #(.width(4)) register_2 (.D(Data), .clk(r1_w), .Q(r1));  // open: en, clr
  Register #(.width(4)) register_3 (.D(Data), .clk(r2_w), .Q(r2));  // open: en, clr
  Register #(.width(4)) register_4 (.D(Data), .clk(r3_w), .Q(r3));  // open: en, clr
  Register #(.width(4)) register_5 (.D(Data), .clk(r4_w), .Q(r4));  // open: en, clr
  Register #(.width(4)) register_6 (.D(Data), .clk(r5_w), .Q(r5));  // open: en, clr
  Register #(.width(4)) register_7 (.D(Data), .clk(r6_w), .Q(r6));  // open: en, clr
  Register #(.width(4)) register_8 (.D(Data), .clk(r7_w), .Q(r7));  // open: en, clr
  Demultiplexer #(.select(3)) demultiplexer_1 (
    .out0(r0_w), .out1(r1_w), .out2(r2_w), .out3(r3_w), .out4(r4_w), .out5(r5_w), .out6(r6_w), .out7(r7_w),
    .in(w), .sel(t[2:0]));
  Multiplexer #(.select(3), .width(4)) multiplexer_1 (
    .in0(r0), .in1(r1), .in2(r2), .in3(r3), .in4(r4), .in5(r5), .in6(r6), .in7(r7), .out(A), .sel(A_in[2:0]));
  Multiplexer #(.select(3), .width(4)) multiplexer_2 (
    .in0(r0), .in1(r1), .in2(r2), .in3(r3), .in4(r4), .in5(r5), .in6(r6), .in7(r7), .out(B), .sel(B_in[2:0]));
endmodule

module PC (
  input  Clock,
  input  DoJump,
  input  IO_in,
  input  RET,
  input  ClockWait,
  input  INT_io,
  output [7:0] CA,
  output [3:0] Operation,
  output [3:0] A_in,
  output [3:0] B_in
);

  wire buffer_1_out, buffer_2_out, buffer_3_out, buffer_4_out, ClockUpd, int_en, LOAD_ADDR, not_2_out,
       or_1_out, register_2_q;
  wire [7:0] multiplexer_1_out, PrevAdress, RET_ADDR;

  or or_1 (or_1_out, LOAD_ADDR, RET, DoJump);
  Multiplexer #(.width(8)) multiplexer_1 (.in0(CA), .in1(RET_ADDR), .out(multiplexer_1_out), .sel(RET));
  Counter #(.ongoal("stay")) counter_1 (
    .load(or_1_out), .clk(ClockUpd), .D(multiplexer_1_out), .Q(PrevAdress));  // open: clr, up, count, carry
  buf buffer_1 (buffer_1_out, IO_in);
  buf buffer_2 (buffer_2_out, buffer_1_out);
  Register #(.width(1)) register_1 (.D(IO_in), .clk(IO_in), .Q(LOAD_ADDR), .clr(INT_io));  // open: en
  Register #(.width(1)) register_2 (.D(IO_in), .en(int_en), .clk(buffer_4_out), .Q(register_2_q), .clr(RET));
  buf buffer_3 (buffer_3_out, buffer_2_out);
  buf buffer_4 (buffer_4_out, buffer_3_out);
  not not_1 (int_en, register_2_q);
  ROM #(.dataWidth(12)) rom_1 (.addr(PrevAdress), .data({Operation, A_in, B_in}));
  Multiplexer #(.width(8)) multiplexer_2 (.in0({A_in, B_in}), .in1(8'hf8), .out(CA), .sel(LOAD_ADDR));
  Register register_3 (.D(PrevAdress), .en(int_en), .clk(IO_in), .Q(RET_ADDR));  // open: clr
  not not_2 (not_2_out, ClockWait);
  and and_1 (ClockUpd, not_2_out, Clock);

  // Other names for the same wires on the sheet: CurrAdress[7:0] = CA

  // Notes on the sheet:
  //   contents of rom_1 (hex, n*v repeats v):
  //   0 13a b03 53 b15 102 630 203 310 b01 910 121 602 930 b13 179 16f 476 b07 102 112 601 c70 634 c70 d78
  //   101 111 601 d78 e80 601 e88 656 e40 f90 76*0 132 14f c17 5*0 135 146 d1a 5*0 102 113 e1f 5*0 155 163
  //   e21 5*0 123 11c 110 120 11d 110 125 11d 110 120 11a 115 125 612 c90 89*0 700 700 16f 376 b07 500 0
  //   500
endmodule

module OperationDecoder (
  input  [3:0] Operation,
  output Digit,
  output Jump,
  output ALULogic,
  output ALU,
  output ALUCarry,
  output FlagWrite,
  output Adress,
  output IO_out,
  output Halt,
  output [3:0] ALUop,
  output INT_io,
  output RET
);

  wire [13:9] rom_1_data;

  ROM #(.addrWidth(4), .dataWidth(16)) rom_1 (
    .addr(Operation),
    .data({RET, INT_io, rom_1_data, Halt, IO_out, Adress, FlagWrite, ALUCarry, ALU, ALULogic, Jump, Digit}));

  assign ALUop = Operation;

  // Notes on the sheet:
  //   contents of rom_1 (hex, n*v repeats v):
  //   0 1 41 40 c 8000 38 4000 100 8 0 c0 4*2
endmodule

module JumpHandler (
  input  a,
  input  b,
  input  c,
  input  d,
  input  JumpOp,
  output DoJump
);

  wire and_1_out, and_2_out, and_3_out, and_4_out, or_1_out;

  and and_1 (and_1_out, a, b, ~c);  // AND_Gate
  and and_2 (and_2_out, ~b, c);  // AND_Gate
  and and_3 (and_3_out, ~a, b, d);  // AND_Gate
  and and_4 (and_4_out, a, ~b, d);  // AND_Gate
  and and_5 (DoJump, or_1_out, JumpOp);
  or or_1 (or_1_out, and_1_out, and_2_out, and_3_out, and_4_out);
endmodule

module IO_2digits (
  input  [3:0] B,
  input  [3:0] A_in,
  input  IO_out,
  input  Write,
  input  Adress,
  output [3:0] first,
  output [3:0] second
);

  wire and_1_out, and_2_out, and_3_out, decoder_1_out0, decoder_1_out1;

  Decoder #(.select(4)) decoder_1 (
    .out0(decoder_1_out0), .out1(decoder_1_out1), .sel(A_in), .en(IO_out));  // open: out2, out3, out4, out5, out6, out7, out8, out9, out10, out11, out12, out13, out14, out15
  and and_1 (and_1_out, IO_out, Adress);
  and and_2 (and_2_out, decoder_1_out0, Write, and_1_out);
  Register #(.width(4)) register_1 (.D(B), .clk(and_2_out), .Q(first));  // open: en, clr
  and and_3 (and_3_out, decoder_1_out1, Write, and_1_out);
  Register #(.width(4)) register_2 (.D(B), .clk(and_3_out), .Q(second));  // open: en, clr

  // Other names for the same wires on the sheet: Data[3:0] = B
endmodule

module IO_buffer (
  input  [3:0] r0,
  input  [3:0] r1,
  input  [3:0] r2,
  input  [3:0] r3,
  input  [3:0] r4,
  input  [3:0] r5,
  input  [3:0] r6,
  input  [3:0] r7,
  input  [3:0] B_in,
  output [3:0] RegData
);

  Multiplexer #(.select(4), .width(4)) multiplexer_1 (
    .in0(r0), .in1(r1), .in2(r2), .in3(r3), .in4(r4), .in5(r5), .in6(r6), .in7(r7), .out(RegData), .sel(B_in));  // open: in8, in9, in10, in11, in12, in13, in14, in15
endmodule
