// Logisim project dragonfly.circ as structural Verilog
module CPU816 (
  input  NotWait,
  input  IntReq,
  input  Reset,
  input  NotClk,
  input  [7:0] DataIn,
  output NotMemWrite,
  output [15:0] Address,
  output NotMemRead,
  output NotIntAck,
  output NotHalt,
  output [7:0] DataOut
);

  wire [63:0] A, B;

  Interface interface_1 (
    .NotWait(NotWait), .IntReq(IntReq), .Reset(Reset), .AIn(A), .NotClk(NotClk), .BIn(B), .DataIn(DataIn),
    .NotMemWrite(NotMemWrite), .AOut(A), .Address(Address), .NotMemRead(NotMemRead), .NotIntAck(NotIntAck),
    .BOut(B), .NotHalt(NotHalt), .DataOut(DataOut));
endmodule

module Interface (
  input  NotWait,
  input  IntReq,
  input  Reset,
  input  [63:0] AIn,
  input  NotClk,
  input  [63:0] BIn,
  input  [7:0] DataIn,
  output NotMemWrite,
  output [63:0] AOut,
  output [15:0] Address,
  output NotMemRead,
  output NotIntAck,
  output [63:0] BOut,
  output NotHalt,
  output [7:0] DataOut
);

  wire n7400_1_pin3, n7400_1_pin6, n7400_1_pin8, n7400_1_pin11, n7400_2_pin2, n7400_2_pin3, n7400_2_pin6,
       n7400_2_pin11, n74193_1_pin4, n74193_1_pin5, n74193_2_pin4, n74193_2_pin5, n74193_2_pin12,
       n74193_2_pin13;

  _7400 u_7400_1 (
    .pin1(AIn[30]), .pin2(BIn[10]), .pin3(n7400_1_pin3), .pin4(AIn[31]), .pin5(BIn[10]), .pin6(n7400_1_pin6),
    .pin13(BIn[60]), .pin12(BIn[9]), .pin11(n7400_1_pin11), .pin10(BIn[61]), .pin9(BIn[9]),
    .pin8(n7400_1_pin8));
  _7400 u_7400_2 (
    .pin1(AIn[14]), .pin2(n7400_2_pin2), .pin3(n7400_2_pin3), .pin4(n7400_2_pin3), .pin5(n7400_2_pin3),
    .pin6(n7400_2_pin6), .pin13(BIn[31]), .pin12(BIn[14]), .pin11(n7400_2_pin11), .pin10(n7400_2_pin11),
    .pin9(n7400_2_pin11), .pin8(n7400_2_pin2));
  _74193 u_74193_1 (
    .pin1(AIn[56]), .pin2(Address[13]), .pin3(Address[12]), .pin4(n74193_1_pin4), .pin5(n74193_1_pin5),
    .pin6(Address[14]), .pin7(Address[15]), .pin15(AIn[55]), .pin14(AIn[5]), .pin11(n7400_1_pin3),
    .pin10(AIn[57]), .pin9(AIn[58]));  // open: pin13, pin12
  _74193 u_74193_2 (
    .pin1(AIn[56]), .pin2(Address[5]), .pin3(Address[4]), .pin4(n74193_2_pin4), .pin5(n74193_2_pin5),
    .pin6(Address[6]), .pin7(Address[7]), .pin15(AIn[55]), .pin14(AIn[5]), .pin13(n74193_2_pin13),
    .pin12(n74193_2_pin12), .pin11(n7400_1_pin6), .pin10(AIn[57]), .pin9(AIn[58]));
  _74193 u_74193_3 (
    .pin1(AIn[52]), .pin2(Address[9]), .pin3(Address[8]), .pin4(n74193_2_pin13), .pin5(n74193_2_pin12),
    .pin6(Address[10]), .pin7(Address[11]), .pin15(AIn[51]), .pin14(AIn[5]), .pin13(n74193_1_pin4),
    .pin12(n74193_1_pin5), .pin11(n7400_1_pin3), .pin10(AIn[53]), .pin9(AIn[54]));
  _74193 u_74193_4 (
    .pin1(AIn[52]), .pin2(Address[1]), .pin3(Address[0]), .pin4(n7400_1_pin11), .pin5(n7400_1_pin8),
    .pin6(Address[2]), .pin7(Address[3]), .pin15(AIn[51]), .pin14(AIn[5]), .pin13(n74193_2_pin4),
    .pin12(n74193_2_pin5), .pin11(n7400_1_pin6), .pin10(AIn[53]), .pin9(AIn[54]));
  _74245 u_74245_1 (
    .pin1(n7400_2_pin11), .pin2(DataIn[0]), .pin3(DataIn[1]), .pin4(DataIn[2]), .pin5(DataIn[3]),
    .pin6(DataIn[4]), .pin7(DataIn[5]), .pin8(DataIn[6]), .pin9(DataIn[7]), .pin19(n7400_2_pin6),
    .pin18(AIn[51]), .pin17(AIn[52]), .pin16(AIn[53]), .pin15(AIn[54]), .pin14(AIn[55]), .pin13(AIn[56]),
    .pin12(AIn[57]), .pin11(AIn[58]));

  assign AOut = AIn;
  assign BOut = BIn;
  assign DataOut = DataIn;
  assign IntReq = AIn[3];
  assign NotClk = BIn[9];
  assign NotHalt = BIn[46];
  assign NotIntAck = BIn[31];
  assign NotMemRead = BIn[14];
  assign NotMemWrite = AIn[14];
  assign NotWait = AIn[4];
  assign Reset = AIn[5];

  // Notes on the sheet:
  //   AddrHigh
  //   AddrLow
  //   ~Clk
  //   Pulse
  //   AddrDec
  //   AddrInc
  //   U1
  //   U5
  //   U5
  //   U6
  //   U6
endmodule
