// Logisim project main.circ as structural Verilog: 13 circuits, main circuit Main
module Main (
);

  wire button_1_out, clock_1_out, clock_2_out, cpu_1_mr, cpu_1_mw, cpu_1_nothalt, dipswitch_1_sw1,
       dipswitch_1_sw2;
  wire [7:0] cpu_1_dataout, ram_1_dout;
  wire [15:0] cpu_1_address;

  Clock #(.highDuration(2), .lowDuration(2)) clock_1 (.out(clock_1_out));
  DipSwitch #(.number(2)) dipswitch_1 (.sw1(dipswitch_1_sw1), .sw2(dipswitch_1_sw2));
  Button button_1 (.out(button_1_out));
  Clock clock_2 (.out(clock_2_out));
  CPU cpu_1 (
    .DataIn(ram_1_dout), .Clk(clock_1_out), .NotReset(dipswitch_1_sw1), .NotWait(dipswitch_1_sw2),
    .Irq(button_1_out), .DataOut(cpu_1_dataout), .NotHalt(cpu_1_nothalt), .MR(cpu_1_mr), .MW(cpu_1_mw),
    .Address(cpu_1_address));  // open: IntAck
  LED led_1 (.in(cpu_1_nothalt));
  RAM #(.addrWidth(16)) ram_1 (
    .addr(cpu_1_address), .we(cpu_1_mw), .oe(cpu_1_mr), .clk(clock_2_out), .din(cpu_1_dataout),
    .dout(ram_1_dout));
endmodule

module StackPointer (
  input  NotReset,
  input  HFromD,
  input  Clk,
  input  HToD,
  input  [7:0] DIn,
  input  LFromD,
  input  NotInc,
  input  LToD,
  input  NotDec,
  output [7:0] DOut
);

  wire and_1_out, counter_2_carry, not_1_out, not_2_out, not_3_out, or_1_out;
  wire [3:0] counter_1_q, counter_1_q_2, counter_2_q, counter_2_q_2;

  not not_1 (not_1_out, NotReset);
  not not_2 (not_2_out, NotInc);
  not not_3 (not_3_out, NotDec);
  or or_1 (or_1_out, not_2_out, not_3_out);
  Counter counter_1 (
    .clr(not_1_out), .load(HFromD), .up(not_2_out), .count(and_1_out), .clk(Clk), .D(DIn),
    .Q({counter_1_q_2, counter_1_q}));  // open: carry
  and and_1 (and_1_out, or_1_out, counter_2_carry);
  Counter counter_2 (
    .clr(not_1_out), .load(LFromD), .up(not_2_out), .count(or_1_out), .clk(Clk), .D(DIn),
    .carry(counter_2_carry), .Q({counter_2_q_2, counter_2_q}));
  assign DOut = HToD ? {counter_1_q_2, counter_1_q} : 8'bz;  // Controlled_Buffer controlled_buffer_1
  assign DOut = LToD ? {counter_2_q_2, counter_2_q} : 8'bz;  // Controlled_Buffer controlled_buffer_2
  Hex_Digit_Display hex_digit_display_1 (.value(counter_1_q_2));  // open: dp
  Hex_Digit_Display hex_digit_display_2 (.value(counter_1_q));  // open: dp
  Hex_Digit_Display hex_digit_display_3 (.value(counter_2_q_2));  // open: dp
  Hex_Digit_Display hex_digit_display_4 (.value(counter_2_q));  // open: dp
endmodule

module CPU (
  input  [7:0] DataIn,
  input  Clk,
  input  NotReset,
  input  NotWait,
  input  Irq,
  output [7:0] DataOut,
  output IntAck,
  output NotHalt,
  output MR,
  output MW,
  output [15:0] Address
);

  wire AccFromD, AccShLeft, AccShRight, AccToD, AddrHFromD, AddrLFromD, ALUCarry, ALUEnable, ALUMode,
       CnstToD, FRFromD, FRToD, FRUpdate, IRFromD, NotAddrDec, NotAddrInc, NotPCInc, NotSPDec, NotSPInc,
       or_1_out, PCHFromD, PCHToD, PCLFromD, PCLToD, SCClear, SPHFromD, SPHToD, SPLFromD, SPLToD, TmpHFromD,
       TmpHToD, TmpLFromD, TmpLToD;
  wire [2:0] alu_1_flagsout, Flags;
  wire [3:0] ALUSel, Step;
  wire [4:0] FromD, ToD;
  wire [7:0] argumentregister_1_hout, argumentregister_1_lout, DBus, Instruction;

  LedBar #(.matrixcols(3)) ledbar_1 (.led0(Flags[0]), .led1(Flags[1]), .led2(Flags[2]));
  Hex_Digit_Display hex_digit_display_1 (.value(Step));  // open: dp
  Hex_Digit_Display hex_digit_display_2 (.value(Instruction[7:4]));  // open: dp
  Hex_Digit_Display hex_digit_display_3 (.value(Instruction[3:0]));  // open: dp
  Hex_Digit_Display hex_digit_display_4 (.value(DBus[7:4]));  // open: dp
  StackPointer stackpointer_1 (
    .NotReset(NotReset), .HFromD(SPHFromD), .Clk(Clk), .HToD(SPHToD), .DIn(DBus), .LFromD(SPLFromD),
    .NotInc(NotSPInc), .LToD(SPLToD), .NotDec(NotSPDec), .DOut(DBus));
  Hex_Digit_Display hex_digit_display_5 (.value(DBus[3:0]));  // open: dp
  RegisterFile registerfile_1 (.DIn(DBus), .FromD(FromD), .ToD(ToD), .NotReset(NotReset), .Clk(Clk), .DOut(DBus));
  ProgramCounter programcounter_1 (
    .NotReset(NotReset), .HFromD(PCHFromD), .Clk(Clk), .HToD(PCHToD), .DIn(DBus), .LFromD(PCLFromD),
    .NotInc(NotPCInc), .LToD(PCLToD), .DOut(DBus));
  InstructionRegister instructionregister_1 (
    .DIn(DBus), .FromD(IRFromD), .Clk(Clk), .NotReset(NotReset), .Instruction(Instruction));
  ArgumentRegister argumentregister_1 (
    .HToD(TmpHToD), .LToD(TmpLToD), .NotReset(NotReset), .HFromD(TmpHFromD), .Clk(Clk), .DIn(DBus),
    .LFromD(TmpLFromD), .DOut(DBus), .HOut(argumentregister_1_hout), .LOut(argumentregister_1_lout));
  Accumulator accumulator_1 (
    .DIn(DBus), .FromD(AccFromD), .ShiftLeft(AccShLeft), .ShiftRight(AccShRight), .Clk(Clk),
    .NotReset(NotReset), .ToD(AccToD), .DOut(DBus));
  assign DBus = CnstToD ? 8'h1c : 8'bz;  // Controlled_Buffer controlled_buffer_1
  ALU alu_1 (
    .AIn(argumentregister_1_hout), .Enable(ALUEnable), .BIn(argumentregister_1_lout), .Sel(ALUSel),
    .Carry(ALUCarry), .Mode(ALUMode), .DOut(DBus), .FlagsOut(alu_1_flagsout));
  AddressRegister addressregister_1 (
    .NotReset(NotReset), .HFromD(AddrHFromD), .Clk(Clk), .DIn(DBus), .LFromD(AddrLFromD),
    .NotInc(NotAddrInc), .NotDec(NotAddrDec), .Address(Address));
  or or_1 (or_1_out, IntAck, MR);
  assign DBus = or_1_out ? DataIn : 8'bz;  // Controlled_Buffer controlled_buffer_2
  assign DataOut = MW ? DBus : 8'bz;  // Controlled_Buffer controlled_buffer_3
  FlagRegister flagregister_1 (
    .FlagsIn(alu_1_flagsout), .DIn(DBus), .FromD(FRFromD), .Update(FRUpdate), .ToD(FRToD), .Clk(Clk),
    .NotReset(NotReset), .FlagsOut(Flags), .DOut(DBus));
  StepCounter stepcounter_1 (
    .Clk(Clk), .NotReset(NotReset), .Clear(SCClear), .NotHalt(NotHalt), .NotWait(NotWait), .Step(Step));
  InstructionDecoder instructiondecoder_1 (
    .Clk(Clk), .IntReq(Irq), .Instruction(Instruction), .Flags(Flags), .Step(Step), .MemFromD(MW),
    .SPHFromD(SPHFromD), .SPLFromD(SPLFromD), .PCHFromD(PCHFromD), .PCLFromD(PCLFromD),
    .TmpHFromD(TmpHFromD), .TmpLFromD(TmpLFromD), .AccFromD(AccFromD), .FRFromD(FRFromD), .IRFromD(IRFromD),
    .AddrHFromD(AddrHFromD), .AddrLFromD(AddrLFromD), .FromD(FromD), .FRUpdate(FRUpdate), .MemToD(MR),
    .ALUCarry(ALUCarry), .SPHToD(SPHToD), .ALUMode(ALUMode), .SPLToD(SPLToD), .PCHToD(PCHToD),
    .PCLToD(PCLToD), .TmpHToD(TmpHToD), .TmpLToD(TmpLToD), .AccToD(AccToD), .FRToD(FRToD), .CnstToD(CnstToD),
    .NotPCInc(NotPCInc), .ALUEnable(ALUEnable), .IntAck(IntAck), .NotHalt(NotHalt), .SCClear(SCClear),
    .ALUSel(ALUSel), .ToD(ToD), .NotSPDec(NotSPDec), .AccShRight(AccShRight), .AccShLeft(AccShLeft),
    .NotSPInc(NotSPInc), .NotAddrDec(NotAddrDec), .NotAddrInc(NotAddrInc));

  // Other names for the same wires on the sheet: IntReq = Irq; MemFromD = MW; MemToD = MR
endmodule

module ArgumentRegister (
  input  HToD,
  input  LToD,
  input  NotReset,
  input  HFromD,
  input  Clk,
  input  [7:0] DIn,
  input  LFromD,
  output [7:0] DOut,
  output [7:0] HOut,
  output [7:0] LOut
);

  wire n74273_1_pin11, n74273_2_pin11;

  _74273 u_74273_1 (
    .pin1(NotReset), .pin2(HOut[0]), .pin3(DIn[0]), .pin4(DIn[1]), .pin5(HOut[1]), .pin6(HOut[2]),
    .pin7(DIn[2]), .pin8(DIn[3]), .pin9(HOut[3]), .pin19(HOut[7]), .pin18(DIn[7]), .pin17(DIn[6]),
    .pin16(HOut[6]), .pin15(HOut[5]), .pin14(DIn[5]), .pin13(DIn[4]), .pin12(HOut[4]), .pin11(n74273_1_pin11));
  and and_1 (n74273_1_pin11, HFromD, Clk);
  _74273 u_74273_2 (
    .pin1(NotReset), .pin2(LOut[0]), .pin3(DIn[0]), .pin4(DIn[1]), .pin5(LOut[1]), .pin6(LOut[2]),
    .pin7(DIn[2]), .pin8(DIn[3]), .pin9(LOut[3]), .pin19(LOut[7]), .pin18(DIn[7]), .pin17(DIn[6]),
    .pin16(LOut[6]), .pin15(LOut[5]), .pin14(DIn[5]), .pin13(DIn[4]), .pin12(LOut[4]), .pin11(n74273_2_pin11));
  assign DOut = HToD ? HOut : 8'bz;  // Controlled_Buffer controlled_buffer_1
  and and_2 (n74273_2_pin11, LFromD, Clk);
  assign DOut = LToD ? LOut : 8'bz;  // Controlled_Buffer controlled_buffer_2
  Hex_Digit_Display hex_digit_display_1 (.value(HOut[7:4]));  // open: dp
  Hex_Digit_Display hex_digit_display_2 (.value(HOut[3:0]));  // open: dp
  Hex_Digit_Display hex_digit_display_3 (.value(LOut[7:4]));  // open: dp
  Hex_Digit_Display hex_digit_display_4 (.value(LOut[3:0]));  // open: dp
endmodule

module Accumulator (
  input  [7:0] DIn,
  input  FromD,
  input  ShiftLeft,
  input  ShiftRight,
  input  Clk,
  input  NotReset,
  input  ToD,
  output [7:0] DOut
);

  wire and_1_out, and_2_out, and_3_out, nor_1_out, not_1_out;
  wire [7:0] register_1_q;

  Register register_1 (.D(DIn), .en(FromD), .clk(Clk), .Q(register_1_q), .clr(not_1_out));
  not not_1 (not_1_out, NotReset);
  and and_1 (and_1_out, ShiftLeft, ToD);
  assign DOut = and_3_out ? {1'b0, register_1_q[7:1]} : 8'bz;  // Controlled_Buffer controlled_buffer_1
  assign DOut = and_1_out ? {register_1_q[6:0], 1'b0} : 8'bz;  // Controlled_Buffer controlled_buffer_2
  assign DOut = and_2_out ? register_1_q : 8'bz;  // Controlled_Buffer controlled_buffer_3
  and and_2 (and_2_out, ToD, nor_1_out);
  nor nor_1 (nor_1_out, ShiftLeft, ShiftRight);
  and and_3 (and_3_out, ShiftRight, ToD);
endmodule

module ALU (
  input  [7:0] AIn,
  input  Enable,
  input  [7:0] BIn,
  input  [3:0] Sel,
  input  Carry,
  input  Mode,
  output [7:0] DOut,
  output [2:0] FlagsOut
);

  wire n74181_1_p13, NotCarry, Sign, Zero;
  wire [6:0] n74181_2_p17;

  // _74181 74181_1: pin names not known; wires that end beside it: BIn[4], AIn[5], AIn[4], BIn[5], Sel[3], AIn[6], Sel[2], BIn[6], Sel[1], AIn[7], Sel[0], BIn[7], n74181_1_p13, Mode, NotCarry, n74181_2_p17[4], n74181_2_p17[5], Sign
  // _74181 74181_2: pin names not known; wires that end beside it: n74181_2_p17[6], BIn[0], AIn[1], AIn[0], BIn[1], Sel[3], AIn[2], Sel[2], BIn[2], Sel[1], AIn[3], Sel[0], BIn[3], Carry, Mode, n74181_1_p13, n74181_2_p17[0], n74181_2_p17[1], n74181_2_p17[2], n74181_2_p17[3]
  nor nor_1 (Zero, Sign, n74181_2_p17[6], n74181_2_p17[5], n74181_2_p17[4], n74181_2_p17[2], n74181_2_p17[0], n74181_2_p17[1], n74181_2_p17[3]);
  assign DOut = Enable ? {Sign, n74181_2_p17} : 8'bz;  // Controlled_Buffer controlled_buffer_1
  assign FlagsOut = Enable ? {Zero, NotCarry, Sign} : 3'bz;  // Controlled_Buffer controlled_buffer_2
endmodule

module FlagRegister (
  input  [2:0] FlagsIn,
  input  [7:0] DIn,
  input  FromD,
  input  Update,
  input  ToD,
  input  Clk,
  input  NotReset,
  output [2:0] FlagsOut,
  output [7:0] DOut
);

  wire not_1_out, or_1_out;
  wire [4:0] controlled_buffer_1_out, register_1_q;

  assign {FlagsIn, controlled_buffer_1_out} = FromD ? DIn : 8'bz;  // Controlled_Buffer controlled_buffer_1
  or or_1 (or_1_out, FromD, Update);
  Register register_1 (
    .D({FlagsIn, controlled_buffer_1_out}), .en(or_1_out), .clk(Clk), .Q({FlagsOut, register_1_q}),
    .clr(not_1_out));
  not not_1 (not_1_out, NotReset);
  assign DOut = ToD ? {FlagsOut, register_1_q} : 8'bz;  // Controlled_Buffer controlled_buffer_2
  // also tied to GND on the sheet: {controlled_buffer_1_out[0], controlled_buffer_1_out[1], controlled_buffer_1_out[2], controlled_buffer_1_out[3], controlled_buffer_1_out[4]}
endmodule

module InstructionRegister (
  input  [7:0] DIn,
  input  FromD,
  input  Clk,
  input  NotReset,
  output [7:0] Instruction
);

  wire not_1_out;

  Register register_1 (.D(DIn), .en(FromD), .clk(Clk), .Q(Instruction), .clr(not_1_out));
  not not_1 (not_1_out, NotReset);
endmodule

module RegisterFile (
  input  [7:0] DIn,
  input  [4:0] FromD,
  input  [4:0] ToD,
  input  NotReset,
  input  Clk,
  output [7:0] DOut
);

  wire decoder_1_out9, decoder_1_out10, decoder_1_out11, decoder_1_out12, decoder_1_out13, not_1_out;
  wire [7:0] register_1_q, register_2_q, register_3_q, register_4_q, register_5_q;

  Decoder #(.select(5)) decoder_1 (
    .out9(decoder_1_out9), .out10(decoder_1_out10), .out11(decoder_1_out11), .out12(decoder_1_out12),
    .out13(decoder_1_out13), .sel(FromD));  // open: out0, out1, out2, out3, out4, out5, out6, out7, out8, out14, out15, out16, out17, out18, out19, out20, out21, out22, out23, out24, out25, out26, out27, out28, out29, out30, out31, en
  not not_1 (not_1_out, NotReset);
  Register register_1 (.D(DIn), .en(decoder_1_out9), .clk(Clk), .Q(register_1_q), .clr(not_1_out));
  Register register_2 (.D(DIn), .en(decoder_1_out10), .clk(Clk), .Q(register_2_q), .clr(not_1_out));
  Register register_3 (.D(DIn), .en(decoder_1_out11), .clk(Clk), .Q(register_3_q), .clr(not_1_out));
  Register register_4 (.D(DIn), .en(decoder_1_out12), .clk(Clk), .Q(register_4_q), .clr(not_1_out));
  Register register_5 (.D(DIn), .en(decoder_1_out13), .clk(Clk), .Q(register_5_q), .clr(not_1_out));
  Multiplexer #(.enable("true"), .select(5), .width(8)) multiplexer_1 (
    .in9(register_1_q), .in10(register_2_q), .in11(register_3_q), .in12(register_4_q), .in13(register_5_q),
    .out(DOut), .sel(ToD));  // open: in0, in1, in2, in3, in4, in5, in6, in7, in8, in14, in15, in16, in17, in18, in19, in20, in21, in22, in23, in24, in25, in26, in27, in28, in29, in30, in31, en
endmodule

module InstructionDecoder (
  input  Clk,
  input  IntReq,
  input  [7:0] Instruction,
  input  [2:0] Flags,
  input  [3:0] Step,
  output MemFromD,
  output SPHFromD,
  output SPLFromD,
  output PCHFromD,
  output PCLFromD,
  output TmpHFromD,
  output TmpLFromD,
  output AccFromD,
  output FRFromD,
  output IRFromD,
  output AddrHFromD,
  output AddrLFromD,
  output [4:0] FromD,
  output FRUpdate,
  output MemToD,
  output ALUCarry,
  output SPHToD,
  output ALUMode,
  output SPLToD,
  output PCHToD,
  output PCLToD,
  output TmpHToD,
  output TmpLToD,
  output AccToD,
  output FRToD,
  output CnstToD,
  output NotPCInc,
  output ALUEnable,
  output IntAck,
  output NotHalt,
  output SCClear,
  output [3:0] ALUSel,
  output [4:0] ToD,
  output NotSPDec,
  output AccShRight,
  output AccShLeft,
  output NotSPInc,
  output NotAddrDec,
  output NotAddrInc
);

  wire IntDisable, IntEnable, j_k_ff_1_q, j_k_ff_1_qn, not_1_out;
  wire [4:4] rom_1_data;
  wire [7:0] rom_3_data;
  wire [7:1] rom_4_data;
  wire [7:5] rom_2_data;
  wire [15:15] nand_1_out;

  nand nand_1 (nand_1_out[15], IntReq, j_k_ff_1_qn);
  not not_1 (not_1_out, IntEnable);
  J_K_Flip_Flop j_k_ff_1 (
    .J(IntDisable), .K(not_1_out), .clk(Clk), .Q(j_k_ff_1_q), .Qn(j_k_ff_1_qn));  // open: preset, reset
  ROM #(.addrWidth(16)) rom_1 (
    .addr({nand_1_out[15], Step, Flags, Instruction}),
    .data({FromD[3], ALUMode, ALUCarry, rom_1_data[4], ToD[0], FromD[0], FromD[1], FromD[2]}));
  ROM #(.addrWidth(16)) rom_2 (
    .addr({nand_1_out[15], Step, Flags, Instruction}),
    .data({rom_2_data[7], NotHalt, rom_2_data[5], ALUSel[0], ALUSel[1], ToD[1], ToD[2], ToD[3]}));
  ROM #(.addrWidth(16)) rom_3 (
    .addr({nand_1_out[15], Step, Flags, Instruction}),
    .data({rom_3_data[7], AccShLeft, AccShRight, FromD[4], ToD[4], ALUSel[2], ALUSel[3], rom_3_data[0]}));
  ROM #(.addrWidth(16)) rom_4 (.addr({nand_1_out[15], Step, Flags, Instruction}), .data({rom_4_data, IntEnable}));
  not not_2 (SCClear, rom_2_data[7]);
  not not_3 (FRUpdate, rom_1_data[4]);
  not not_4 (NotSPDec, rom_3_data[0]);
  not not_5 (NotSPInc, rom_3_data[7]);
  not not_6 (NotPCInc, rom_2_data[5]);
  not not_7 (IntDisable, rom_4_data[1]);
  not not_8 (NotAddrDec, rom_4_data[2]);
  not not_9 (NotAddrInc, rom_4_data[3]);
  Decoder #(.select(5)) decoder_1 (
    .out1(MemFromD), .out2(SPHFromD), .out3(SPLFromD), .out4(PCHFromD), .out5(PCLFromD), .out6(TmpHFromD),
    .out7(TmpLFromD), .out8(AccFromD), .out14(FRFromD), .out15(IRFromD), .out16(AddrHFromD),
    .out17(AddrLFromD), .sel(FromD));  // open: out0, out9, out10, out11, out12, out13, out18, out19, out20, out21, out22, out23, out24, out25, out26, out27, out28, out29, out30, out31, en
  Decoder #(.select(5)) decoder_2 (
    .out1(MemToD), .out2(SPHToD), .out3(SPLToD), .out4(PCHToD), .out5(PCLToD), .out6(TmpHToD),
    .out7(TmpLToD), .out8(AccToD), .out14(FRToD), .out15(CnstToD), .out16(ALUEnable), .out17(IntAck),
    .sel(ToD));  // open: out0, out9, out10, out11, out12, out13, out18, out19, out20, out21, out22, out23, out24, out25, out26, out27, out28, out29, out30, out31, en

  // Other names for the same wires on the sheet: FromDBus[4:0] = FromD; ToDBus[4:0] = ToD

  // Notes on the sheet:
  //   contents of rom_1 (hex, n*v repeats v):
  //   bf 20*30 5*38 8*30 5*38 b4 b2 b6 b3 b1 b5 b8 ba be bb b9 bd b0 b4 b6 b3 b1 b5 b8 bc ba bb b9 bd b0
  //   b4 b2 b6 b1 b5 b0 b4 b2 b6 b3 b5 b8 bc ba be bb b9 3a b5 b5 22*30 39 4*bf 30 39 30 39 bf bf 30 39 30
  //   bf bf 30 30 bf 30 30 bf bf 30 30 bf 30 37 3f 37 3f 37 3f 30 37 3f 37 3f 37 3f 30 37 3f 37 3f 37 3f
  //   30 37 3f 37 3f 37 3f 30 37 3f 37 3f 37 3f 30 37 3f 37 3f 37 3f 30 37 3f 37 3f 37 3f 30 33 3b 33 3b
  //   33 3b 33 3b 33 3b 33 3b 33 3b 33 3b 33 3b 33 3b 33 3b 33 3b 33 3b 33 3b 33 3b 37 3f 37 3f 37 3f 30
  //   b0 b0 30 34*0 bf 20*30 5*38 8*30 5*38 b4 b2 b6 b3 b1 b5 b8 ba be bb b9 bd b0 b4 b6 b3 b1 b5 b8 bc ba
  //   bb b9 bd b0 b4 b2 b6 b1 b5 b0 b4 b2 b6 b3 b5 b8 bc ba be bb b9 3a b5 b5 22*30 39 4*bf 30 39 bf bf 30
  //   39 30 39 30 bf bf 30 bf 30 30 30 bf bf 30 bf 30 30 37 3f 37 3f 37 3f 30 37 3f 37 3f 37 3f 30 37 3f
  //   37 3f 37 3f 30 37 3f 37 3f 37 3f 30 37 3f 37 3f 37 3f 30 37 3f 37 3f 37 3f 30 37 3f 37 3f 37 3f 30
  //   33 3b 33 3b 33 3b 33 3b 33 3b 33 3b 33 3b 33 3b 33 3b 33 3b 33 3b 33 3b 33 3b 33 3b 33 3b 37 3f 37
  //   3f 37 3f 30 b0 b0 30 34*0 bf 20*30 5*38 8*30 5*38 b4 b2 b6 b3 b1 b5 b8 ba be bb b9 bd b0 b4 b6 b3 b1
  //   b5 b8 bc ba bb b9 bd b0 b4 b2 b6 b1 b5 b0 b4 b2 b6 b3 b5 b8 bc ba be bb b9 3a b5 b5 22*30 39 bf bf
  //   30 39 bf bf 30 39 bf bf 30 39 30 bf 30 bf 30 bf 30 30 bf 30 bf 30 bf 30 37 3f 37 3f 37 3f 30 37 3f
  //   37 3f 37 3f 30 37 3f 37 3f 37 3f 30 37 3f 37 3f 37 3f 30 37 3f 37 3f 37 3f 30 37 3f 37 3f 37 3f 30
  //   37 3f 37 3f 37 3f 30 33 3b 33 3b 33 3b 33 3b 33 3b 33 3b 33 3b 33 3b 33 3b 33 3b 33 3b 33 3b 33 3b
  //   33 3b 33 3b 37 3f 37 3f 37 3f 30 b0 b0 30 34*0 bf 20*30 5*38 8*30 5*38 b4 b2 b6 b3 b1 b5 b8 ba be bb
  //   b9 bd b0 b4 b6 b3 b1 b5 b8 bc ba bb b9 bd b0 b4 b2 b6 b1 b5 b0 b4 b2 b6 b3 b5 b8 bc ba be bb b9 3a
  //   b5 b5 22*30 39 bf bf 30 39 4*bf 30 39 30 39 30 bf 30 bf bf 30 30 30 bf 30 bf bf 30 30 37 3f 37 3f 37
  //   3f 30 37 3f 37 3f 37 3f 30 37 3f 37 3f 37 3f 30 37 3f 37 3f 37 3f 30 37 3f 37 3f 37 3f 30 37 3f 37
  //   3f 37 3f 30 37 3f 37 3f 37 3f 30 33 3b 33 3b 33 3b 33 3b 33 3b 33 3b 33 3b 33 3b 33 3b 33 3b 33 3b
  //   33 3b 33 3b 33 3b 33 3b 37 3f 37 3f 37 3f 30 b0 b0 30 34*0 bf 20*30 5*38 8*30 5*38 b4 b2 b6 b3 b1 b5
  //   b8 ba be bb b9 bd b0 b4 b6 b3 b1 b5 b8 bc ba bb b9 bd b0 b4 b2 b6 b1 b5 b0 b4 b2 b6 b3 b5 b8 bc ba
  //   be bb b9 3a b5 b5 21*30 bf bf 30 39 bf bf 30 39 30 39 bf bf 30 39 bf 30 bf 30 30 bf 30 bf 30 bf 30
  //   30 bf 30 37 3f 37 3f 37 3f 30 37 3f 37 3f 37 3f 30 37 3f 37 3f 37 3f 30 37 3f 37 3f 37 3f 30 37 3f
  //   37 3f 37 3f 30 37 3f 37 3f 37 3f 30 37 3f 37 3f 37 3f 30 33 3b 33 3b 33 3b 33 3b 33 3b 33 3b 33 3b
  //   33 3b 33 3b 33 3b 33 3b 33 3b 33 3b 33 3b 33 3b 37 3f 37 3f 37 3f 30 b0 b0 30 34*0 bf 20*30 5*38
  //   8*30 5*38 b4 b2 b6 b3 b1 b5 b8 ba be bb b9 bd b0 b4 b6 b3 b1 b5 b8 bc ba bb b9 bd b0 b4 b2 b6 b1 b5
  //   b0 b4 b2 b6 b3 b5 b8 bc ba be bb b9 3a b5 b5 21*30 bf bf 30 39 bf bf 30 39 bf bf 30 39 30 39 bf 30
  //   bf 30 bf 30 30 bf 30 bf 30 bf 30 30 37 3f 37 3f 37 3f 30 37 3f 37 3f 37 3f 30 37 3f 37 3f 37 3f 30
  //   37 3f 37 3f 37 3f 30 37 3f 37 3f 37 3f 30 37 3f 37 3f 37 3f 30 37 3f 37 3f 37 3f 30 33 3b 33 3b 33
  //   3b 33 3b 33 3b 33 3b 33 3b 33 3b 33 3b 33 3b 33 3b 33 3b 33 3b 33 3b 33 3b 37 3f 37 3f 37 3f 30 b0
  //   b0 30 34*0 bf 20*30 5*38 8*30 5*38 b4 b2 b6 b3 b1 b5 b8 ba be bb b9 bd b0 b4 b6 b3 b1 b5 b8 bc ba bb
  //   b9 bd b0 b4 b2 b6 b1 b5 b0 b4 b2 b6 b3 b5 b8 bc ba be bb b9 3a b5 b5 21*30 bf bf 30 39 30 39 bf bf
  //   30 39 bf bf 30 39 bf 30 30 bf 30 bf 30 bf 30 30 bf 30 bf 30 37 3f 37 3f 37 3f 30 37 3f 37 3f 37 3f
  //   30 37 3f 37 3f 37 3f 30 37 3f 37 3f 37 3f 30 37 3f 37 3f 37 3f 30 37 3f 37 3f 37 3f 30 37 3f 37 3f
  //   37 3f 30 33 3b 33 3b 33 3b 33 3b 33 3b 33 3b 33 3b 33 3b 33 3b 33 3b 33 3b 33 3b 33 3b 33 3b 33 3b
  //   37 3f 37 3f 37 3f 30 b0 b0 30 34*0 bf 20*30 5*38 8*30 5*38 b4 b2 b6 b3 b1 b5 b8 ba be bb b9 bd b0 b4
  //   b6 b3 b1 b5 b8 bc ba bb b9 bd b0 b4 b2 b6 b1 b5 b0 b4 b2 b6 b3 b5 b8 bc ba be bb b9 3a b5 b5 21*30
  //   bf bf 30 39 30 39 4*bf 30 39 30 39 bf 30 30 bf bf 30 30 bf 30 30 bf bf 30 30 37 3f 37 3f 37 3f 30 37
  //   3f 37 3f 37 3f 30 37 3f 37 3f 37 3f 30 37 3f 37 3f 37 3f 30 37 3f 37 3f 37 3f 30 37 3f 37 3f 37 3f
  //   30 37 3f 37 3f 37 3f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
  //   contents of rom_2 (hex, n*v repeats v):
  //   47 c0 c0 18*c2 5*c3 c2 c2 c4 5*c2 5*c3 12*c1 12*c5 6*c7 13*c3 c4 c2 11*c4 10*c0 c2 c3 4*47 c2 c3 c2
  //   c3 47 47 c2 c3 c2 47 47 c2 c2 47 c2 c0 47 47 c0 c0 47 c0 c1 c1 c5 c5 c3 c3 c2 c1 c1 c5 c5 c3 c3 c2
  //   c1 c1 c5 c5 c3 c3 c2 c1 c1 c5 c5 c3 c3 c2 c1 c1 c5 c5 c3 c3 c2 c1 c1 c5 c5 c3 c3 c2 c1 c1 c5 c5 c3
  //   c3 c2 c1 c1 c5 c5 c3 c3 c1 c1 c5 c5 c3 c3 c1 c1 c5 c5 c3 c3 c1 c1 c5 c5 c3 c3 c1 c1 c5 c5 c3 c3 c1
  //   c1 c5 c5 c3 c3 c2 c1 c1 80 34*0 47 c0 c0 18*c2 5*c3 c2 c2 c4 5*c2 5*c3 12*c1 12*c5 6*c7 13*c3 c4 c2
  //   11*c4 10*c0 c2 c3 4*47 c2 c3 47 47 c2 c3 c2 c3 c2 47 47 c2 47 c2 c2 c0 47 47 c0 47 c0 c0 c1 c1 c5 c5
  //   c3 c3 c2 c1 c1 c5 c5 c3 c3 c2 c1 c1 c5 c5 c3 c3 c2 c1 c1 c5 c5 c3 c3 c2 c1 c1 c5 c5 c3 c3 c2 c1 c1
  //   c5 c5 c3 c3 c2 c1 c1 c5 c5 c3 c3 c2 c1 c1 c5 c5 c3 c3 c1 c1 c5 c5 c3 c3 c1 c1 c5 c5 c3 c3 c1 c1 c5
  //   c5 c3 c3 c1 c1 c5 c5 c3 c3 c1 c1 c5 c5 c3 c3 c2 c1 c1 80 34*0 47 c0 c0 18*c2 5*c3 c2 c2 c4 5*c2 5*c3
  //   12*c1 12*c5 6*c7 13*c3 c4 c2 11*c4 10*c0 c2 c3 47 47 c2 c3 47 47 c2 c3 47 47 c2 c3 c2 47 c2 47 c2 47
  //   c2 c0 47 c0 47 c0 47 c0 c1 c1 c5 c5 c3 c3 c2 c1 c1 c5 c5 c3 c3 c2 c1 c1 c5 c5 c3 c3 c2 c1 c1 c5 c5
  //   c3 c3 c2 c1 c1 c5 c5 c3 c3 c2 c1 c1 c5 c5 c3 c3 c2 c1 c1 c5 c5 c3 c3 c2 c1 c1 c5 c5 c3 c3 c1 c1 c5
  //   c5 c3 c3 c1 c1 c5 c5 c3 c3 c1 c1 c5 c5 c3 c3 c1 c1 c5 c5 c3 c3 c1 c1 c5 c5 c3 c3 c2 c1 c1 80 34*0 47
  //   c0 c0 18*c2 5*c3 c2 c2 c4 5*c2 5*c3 12*c1 12*c5 6*c7 13*c3 c4 c2 11*c4 10*c0 c2 c3 47 47 c2 c3 4*47
  //   c2 c3 c2 c3 c2 47 c2 47 47 c2 c2 c0 47 c0 47 47 c0 c0 c1 c1 c5 c5 c3 c3 c2 c1 c1 c5 c5 c3 c3 c2 c1
  //   c1 c5 c5 c3 c3 c2 c1 c1 c5 c5 c3 c3 c2 c1 c1 c5 c5 c3 c3 c2 c1 c1 c5 c5 c3 c3 c2 c1 c1 c5 c5 c3 c3
  //   c2 c1 c1 c5 c5 c3 c3 c1 c1 c5 c5 c3 c3 c1 c1 c5 c5 c3 c3 c1 c1 c5 c5 c3 c3 c1 c1 c5 c5 c3 c3 c1 c1
  //   c5 c5 c3 c3 c2 c1 c1 80 34*0 47 c0 c0 18*c2 5*c3 c2 c2 c4 5*c2 5*c3 12*c1 12*c5 6*c7 13*c3 c4 c2
  //   11*c4 10*c0 47 47 c2 c3 47 47 c2 c3 c2 c3 47 47 c2 c3 47 c2 47 c2 c2 47 c2 47 c0 47 c0 c0 47 c0 c1
  //   c1 c5 c5 c3 c3 c2 c1 c1 c5 c5 c3 c3 c2 c1 c1 c5 c5 c3 c3 c2 c1 c1 c5 c5 c3 c3 c2 c1 c1 c5 c5 c3 c3
  //   c2 c1 c1 c5 c5 c3 c3 c2 c1 c1 c5 c5 c3 c3 c2 c1 c1 c5 c5 c3 c3 c1 c1 c5 c5 c3 c3 c1 c1 c5 c5 c3 c3
  //   c1 c1 c5 c5 c3 c3 c1 c1 c5 c5 c3 c3 c1 c1 c5 c5 c3 c3 c2 c1 c1 80 34*0 47 c0 c0 18*c2 5*c3 c2 c2 c4
  //   5*c2 5*c3 12*c1 12*c5 6*c7 13*c3 c4 c2 11*c4 10*c0 47 47 c2 c3 47 47 c2 c3 47 47 c2 c3 c2 c3 47 c2
  //   47 c2 47 c2 c2 47 c0 47 c0 47 c0 c0 c1 c1 c5 c5 c3 c3 c2 c1 c1 c5 c5 c3 c3 c2 c1 c1 c5 c5 c3 c3 c2
  //   c1 c1 c5 c5 c3 c3 c2 c1 c1 c5 c5 c3 c3 c2 c1 c1 c5 c5 c3 c3 c2 c1 c1 c5 c5 c3 c3 c2 c1 c1 c5 c5 c3
  //   c3 c1 c1 c5 c5 c3 c3 c1 c1 c5 c5 c3 c3 c1 c1 c5 c5 c3 c3 c1 c1 c5 c5 c3 c3 c1 c1 c5 c5 c3 c3 c2 c1
  //   c1 80 34*0 47 c0 c0 18*c2 5*c3 c2 c2 c4 5*c2 5*c3 12*c1 12*c5 6*c7 13*c3 c4 c2 11*c4 10*c0 47 47 c2
  //   c3 c2 c3 47 47 c2 c3 47 47 c2 c3 47 c2 c2 47 c2 47 c2 47 c0 c0 47 c0 47 c0 c1 c1 c5 c5 c3 c3 c2 c1
  //   c1 c5 c5 c3 c3 c2 c1 c1 c5 c5 c3 c3 c2 c1 c1 c5 c5 c3 c3 c2 c1 c1 c5 c5 c3 c3 c2 c1 c1 c5 c5 c3 c3
  //   c2 c1 c1 c5 c5 c3 c3 c2 c1 c1 c5 c5 c3 c3 c1 c1 c5 c5 c3 c3 c1 c1 c5 c5 c3 c3 c1 c1 c5 c5 c3 c3 c1
  //   c1 c5 c5 c3 c3 c1 c1 c5 c5 c3 c3 c2 c1 c1 80 34*0 47 c0 c0 18*c2 5*c3 c2 c2 c4 5*c2 5*c3 12*c1 12*c5
  //   6*c7 13*c3 c4 c2 11*c4 10*c0 47 47 c2 c3 c2 c3 4*47 c2 c3 c2 c3 47 c2 c2 47 47 c2 c2 47 c0 c0 47 47
  //   c0 c0 c1 c1 c5 c5 c3 c3 c2 c1 c1 c5 c5 c3 c3 c2 c1 c1 c5 c5 c3 c3 c2 c1 c1 c5 c5 c3 c3 c2 c1 c1 c5
  //   c5 c3 c3 c2 c1 c1 c5 c5 c3 c3 c2 c1 c1 c5 c5 c3 c3 c2 c1 c1 c5 c5 c3 c3 c1 c1 c5 c5 c3 c3 c1 c1 c5
  //   c5 c3 c3 c1 c1 c5 c5 c3 c3 c1 c1 c5 c5 c3 c3 c1 c1 c5 c5 c3 c3 c2 c1 c1 80 34*0 c2 47 47 18*c2 5*c3
  //   c2 c2 c4 5*c2 5*c3 42*47 c3 c4 c2 21*c4 c2 c3 5*c2 c3 c2 c3 c2 c2 c2 c3 7*c2 c4 c2 c2 c4 c4 c2 c4
  //   6*c1 c2 6*c1 c2 6*c1 c2 6*c1 c2 6*c1 c2 6*c1 c2 6*c1 c2 6*c0 6*d8 6*c0 6*d8 6*c0 6*c1 c2 47 47 35*0
  //   c2 47 47 18*c2 5*c3 c2 c2 c4 5*c2 5*c3 42*47 c3 c4 c2 21*c4 c2 c3 5*c2 c3 c2 c2 c2 c3 c2 c3 7*c2 c4
  //   c2 c2 c4 c2 c4 c4 6*c1 c2 6*c1 c2 6*c1 c2 6*c1 c2 6*c1 c2 6*c1 c2 6*c1 c2 6*c0 6*d8 6*c0 6*d8 6*c0
  //   6*c1 c2 47 47 35*0 c2 47 47 18*c2 5*c3 c2 c2 c4 5*c2 5*c3 42*47 c3 c4 c2 21*c4 c2 c3 c2 c2 c2 c3 c2
  //   c2 c2 c3 c2 c2 c2 c3 7*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
  //   contents of rom_3 (hex, n*v repeats v):
  //   0 0 0 36*10 45*0 11*10 10*80 10 5*0 10 0 10 0 0 0 10 0 10 0 0 10 10 0 10 80 0 0 80 80 0 80 6*0 10
  //   6*0 10 6*0 10 6*0 10 6*0 10 6*0 10 6*0 10 36*0 10 40 20 38*0 36*10 45*0 11*10 10*80 10 5*0 10 0 0 0
  //   10 0 10 0 10 0 0 10 0 10 10 80 0 0 80 0 80 80 6*0 10 6*0 10 6*0 10 6*0 10 6*0 10 6*0 10 6*0 10 36*0
  //   10 40 20 38*0 36*10 45*0 11*10 10*80 10 0 0 0 10 0 0 0 10 0 0 0 10 0 10 0 10 0 10 0 10 80 0 80 0 80
  //   0 80 6*0 10 6*0 10 6*0 10 6*0 10 6*0 10 6*0 10 6*0 10 36*0 10 40 20 38*0 36*10 45*0 11*10 10*80 10 0
  //   0 0 10 5*0 10 0 10 0 10 0 10 0 0 10 10 80 0 80 0 0 80 80 6*0 10 6*0 10 6*0 10 6*0 10 6*0 10 6*0 10
  //   6*0 10 36*0 10 40 20 38*0 36*10 45*0 11*10 10*80 0 0 10 0 0 0 10 0 10 0 0 0 10 0 0 10 0 10 10 0 10 0
  //   80 0 80 80 0 80 6*0 10 6*0 10 6*0 10 6*0 10 6*0 10 6*0 10 6*0 10 36*0 10 40 20 38*0 36*10 45*0 11*10
  //   10*80 0 0 10 0 0 0 10 0 0 0 10 0 10 0 0 10 0 10 0 10 10 0 80 0 80 0 80 80 6*0 10 6*0 10 6*0 10 6*0
  //   10 6*0 10 6*0 10 6*0 10 36*0 10 40 20 38*0 36*10 45*0 11*10 10*80 0 0 10 0 10 0 0 0 10 0 0 0 10 0 0
  //   10 10 0 10 0 10 0 80 80 0 80 0 80 6*0 10 6*0 10 6*0 10 6*0 10 6*0 10 6*0 10 6*0 10 36*0 10 40 20
  //   38*0 36*10 45*0 11*10 10*80 0 0 10 0 10 5*0 10 0 10 0 0 10 10 0 0 10 10 0 80 80 0 0 80 80 6*0 10 6*0
  //   10 6*0 10 6*0 10 6*0 10 6*0 10 6*0 10 36*0 10 40 20 35*0 10 0 0 36*10 45*0 22*10 0 5*10 0 10 0 10 10
  //   10 0 14*10 6*0 10 6*0 10 6*0 10 6*0 10 6*0 10 6*0 10 6*0 10 6*8 6*e 6*8 6*e 6*8 6*0 10 37*0 10 0 0
  //   36*10 45*0 22*10 0 5*10 0 10 10 10 0 10 0 14*10 6*0 10 6*0 10 6*0 10 6*0 10 6*0 10 6*0 10 6*0 10 6*8
  //   6*e 6*8 6*e 6*8 6*0 10 37*0 10 0 0 36*10 45*0 22*10 0 10 10 10 0 10 10 10 0 10 10 10 0 14*10 6*0 10
  //   6*0 10 6*0 10 6*0 10 6*0 10 6*0 10 6*0 10 6*8 6*e 6*8 6*e 6*8 6*0 10 37*0 10 0 0 36*10 45*0 22*10 0
  //   10 10 10 0 5*10 0 10 0 14*10 6*0 10 6*0 10 6*0 10 6*0 10 6*0 10 6*0 10 6*0 10 6*8 6*e 6*8 6*e 6*8
  //   6*0 10 37*0 10 0 0 36*10 45*0 24*10 0 10 10 10 0 10 0 10 10 10 0 14*10 6*0 10 6*0 10 6*0 10 6*0 10
  //   6*0 10 6*0 10 6*0 10 6*8 6*e 6*8 6*e 6*8 6*0 10 37*0 10 0 0 36*10 45*0 24*10 0 10 10 10 0 10 10 10 0
  //   10 0 14*10 6*0 10 6*0 10 6*0 10 6*0 10 6*0 10 6*0 10 6*0 10 6*8 6*e 6*8 6*e 6*8 6*0 10 37*0 10 0 0
  //   36*10 45*0 24*10 0 10 0 10 10 10 0 10 10 10 0 14*10 6*0 10 6*0 10 6*0 10 6*0 10 6*0 10 6*0 10 6*0 10
  //   6*8 6*e 6*8 6*e 6*8 6*0 10 37*0 10 0 0 36*10 45*0 24*10 0 10 0 5*10 0 10 0 14*10 6*0 10 6*0 10 6*0
  //   10 6*0 10 6*0 10 6*0 10 6*0 10 6*8 6*e 6*8 6*e 6*8 6*0 10 38*0 10 10 25*0 1 10*0 42*10 0 0 0 11*1
  //   10*10 21*0 10 0 0 10 10 0 10 6*a 0 6*c 0 6*c 0 6*c 0 6*8 0 6*a 0 6*c 31*0 6*c 0 10 10 36*0 10 10
  //   25*0 1 10*0 42*10 0 0 0 11*1 10*10 21*0 10 0 0 10 0 10 10 6*a 0 6*c 0 6*c 0 6*c 0 6*8 0 6*a 0 6*c
  //   31*0 6*c 0 10 10 36*0 10 10 25*0 1 10*0 42*10 0 0 0 11*1 10*10 21*0 10 0 10 0 10 0 10 6*a 0 6*c 0
  //   6*c 0 6*c 0 6*8 0 6*a 0 6*c 31*0 6*c 0 10 10 36*0 10 10 25*0 1 10*0 42*10 0 0 0 11*1 10*10 21*0 10 0
  //   10 0 0 10 10 6*a 0 6*c 0 6*c 0 6*c 0 6*8 0 6*a 0 6*c 31*0 6*c 0 10 10 36*0 10 10 25*0 1 10*0 42*10 0
  //   0 0 11*1 10*10 22*0 10 0 10 10 0 10 6*a 0 6*c 0 6*c 0 6*c 0 6*8 0 6*a 0 6*c 31*0 6*c 0 10 10 36*0 10
  //   10 25*0 1 10*0 42*10 0 0 0 11*1 10*10 22*0 10 0 10 0 10 10 6*a 0 6*c 0 6*c 0 6*c 0 6*8 0 6*a 0 6*c
  //   31*0 6*c 0 10 10 36*0 10 10 25*0 1 10*0 42*10 0 0 0 11*1 10*10 22*0 10 10 0 10 0 10 6*a 0 6*c 0 6*c
  //   0 6*c 0 6*8 0 6*a 0 6*c 31*0 6*c 0 10 10 36*0 10 10 25*0 1 10*0 42*10 0 0 0 11*1 10*10 22*0 10 10 0
  //   0 10 10 6*a 0 6*c 0 6*c 0 6*c 0 6*8 0 6*a 0 6*c 31*0 6*c 0 10 10 63*0 1 52*0 10 10 10 7*0 4*1 10*80
  //   0 10 5*0 10 0 10 0 0 0 10 7*0 80 0 0 80 80 0 80 49*0 30*10 72*0 1 52*0 10 10 10 7*0 4*1 10*80 0 10
  //   5*0 10 0 0 0 10 0 10 7*0 80 0 0 80 0 80 80 49*0 30*10 72*0 1 52*0 10 10 10 7*0 4*1 10*80 0 10 0 0 0
  //   10 0 0 0 10 0 0 0 10 7*0 80 0 80 0 80 0 80 49*0 30*10 72*0 1 52*0 10 10 10 7*0 4*1 10*80 0 10 0 0 0
  //   10 5*0 10 0 10 7*0 80 0 80 0 0 80 80 49*0 30*10 72*0 1 52*0 10 10 10 7*0 4*1 10*80 0 0 0 10 0 0 0 10
  //   0 10 0 0 0 10 8*0 80 0 80 80 0 80 49*0 30*10 72*0 1 52*0 10 10 10 7*0 4*1 10*80 0 0 0 10 0 0 0 10 0
  //   0 0 10 0 10 8*0 80 0 80 0 80 80 49*0 30*10 72*0 1 52*0 10 10 10 7*0 4*1 10*80 0 0 0 10 0 10 0 0 0 10
  //   0 0 0 10 8*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
  //   contents of rom_4 (hex, n*v repeats v):
  //   3 2 1 219*3 34*0 3 2 1 219*3 34*0 3 2 1 219*3 34*0 3 2 1 219*3 34*0 3 2 1 219*3 34*0 3 2 1 219*3
  //   34*0 3 2 1 219*3 34*0 3 2 1 219*3 34*0 221*3 35*0 221*3 35*0 221*3 35*0 221*3 35*0 221*3 35*0 221*3
  //   35*0 221*3 35*0 221*3 35*0 3 3 3 18*b 5*3 b b 7 5*b 50*3 11*7 10*3 b 5*3 b 3 b 3 3 3 b 3 b 3 3 b b 3
  //   b 13*3 b 6*3 b 6*3 b 6*3 b 6*3 b 6*3 b 6*3 b 36*3 b 3 3 35*0 3 3 3 18*b 5*3 b b 7 5*b 50*3 11*7 10*3
  //   b 5*3 b 3 3 3 b 3 b 3 b 3 3 b 3 b b 13*3 b 6*3 b 6*3 b 6*3 b 6*3 b 6*3 b 6*3 b 36*3 b 3 3 35*0 3 3 3
  //   18*b 5*3 b b 7 5*b 50*3 11*7 10*3 b 3 3 3 b 3 3 3 b 3 3 3 b 3 b 3 b 3 b 3 b 13*3 b 6*3 b 6*3 b 6*3 b
  //   6*3 b 6*3 b 6*3 b 36*3 b 3 3 35*0 3 3 3 18*b 5*3 b b 7 5*b 50*3 11*7 10*3 b 3 3 3 b 5*3 b 3 b 3 b 3
  //   b 3 3 b b 13*3 b 6*3 b 6*3 b 6*3 b 6*3 b 6*3 b 6*3 b 36*3 b 3 3 35*0 3 3 3 18*b 5*3 b b 7 5*b 50*3
  //   11*7 12*3 b 3 3 3 b 3 b 3 3 3 b 3 3 b 3 b b 3 b 13*3 b 6*3 b 6*3 b 6*3 b 6*3 b 6*3 b 6*3 b 36*3 b 3
  //   3 35*0 3 3 3 18*b 5*3 b b 7 5*b 50*3 11*7 12*3 b 3 3 3 b 3 3 3 b 3 b 3 3 b 3 b 3 b b 13*3 b 6*3 b
  //   6*3 b 6*3 b 6*3 b 6*3 b 6*3 b 36*3 b 3 3 35*0 3 3 3 18*b 5*3 b b 7 5*b 50*3 11*7 12*3 b 3 b 3 3 3 b
  //   3 3 3 b 3 3 b b 3 b 3 b 13*3 b 6*3 b 6*3 b 6*3 b 6*3 b 6*3 b 6*3 b 36*3 b 3 3 35*0 3 3 3 18*b 5*3 b
  //   b 7 5*b 50*3 11*7 12*3 b 3 b 5*3 b 3 b 3 3 b b 3 3 b b 13*3 b 6*3 b 6*3 b 6*3 b 6*3 b 6*3 b 6*3 b
  //   36*3 b 3 3 36*0 94*3 10*b 3 3 4*0 4*3 0 0 3 3 3 0 0 3 3 0 3 b 0 0 b b 0 b 88*3 36*0 94*3 10*b 3 3
  //   4*0 3 3 0 0 5*3 0 0 3 0 3 3 b 0 0 b 0 b b 88*3 36*0 94*3 10*b 3 3 0 0 3 3 0 0 3 3 0 0 3 3 3 0 3 0 3
  //   0 3 b 0 b 0 b 0 b 88*3 36*0 94*3 10*b 3 3 0 0 3 3 4*0 5*3 0 3 0 0 3 3 b 0 b 0 0 b b 88*3 36*0 94*3
  //   10*b 0 0 3 3 0 0 4*3 0 0 3 3 0 3 0 3 3 0 3 0 b 0 b b 0 b 88*3 36*0 94*3 10*b 0 0 3 3 0 0 3 3 0 0 4*3
  //   0 3 0 3 0 3 3 0 b 0 b 0 b b 88*3 36*0 94*3 10*b 0 0 4*3 0 0 3 3 0 0 3 3 0 3 3 0 3 0 3 0 b b 0 b 0 b
  //   88*3 36*0 94*3 10*b 0 0 4*3 4*0 4*3 0 3 3 0 0 3 3 0 b b 0 0 b b 88*3 38*0 36*3 42*0 26*3 4*0 4*3 0 0
  //   3 3 3 0 0 3 3 0 3 3 0 0 3 3 0 87*3 40*0 36*3 42*0 26*3 4*0 3 3 0 0 5*3 0 0 3 0 3 3 3 0 0 3 0 88*3
  //   40*0 36*3 42*0 26*3 0 0 3 3 0 0 3 3 0 0 3 3 3 0 3 0 3 0 3 3 0 3 0 3 0 87*3 40*0 36*3 42*0 26*3 0 0 3
  //   3 4*0 5*3 0 3 0 0 3 3 3 0 3 0 0 88*3 40*0 36*3 42*0 24*3 0 0 3 3 0 0 4*3 0 0 3 3 0 3 0 3 3 0 3 0 3 0
  //   3 3 0 87*3 40*0 36*3 42*0 24*3 0 0 3 3 0 0 3 3 0 0 4*3 0 3 0 3 0 3 3 0 3 0 3 0 88*3 40*0 36*3 42*0
  //   24*3 0 0 4*3 0 0 3 3 0 0 3 3 0 3 3 0 3 0 3 0 3 3 0 3 0 87*3 40*0 36*3 42*0 24*3 0 0 4*3 4*0 4*3 0 3
  //   3 0 0 3 3 0 3 3 0 0 88*3 40*0 36*3 45*0 22*3 5*0 3 0 3 0 0 0 3 0 3 0 0 3 3 0 3 3 0 0 3 3 0 50*3 30*0
  //   7*3 40*0 36*3 45*0 22*3 5*0 3 0 0 0 3 0 3 0 3 0 0 3 0 3 3 3 0 0 3 0 51*3 30*0 7*3 40*0 36*3 45*0
  //   22*3 0 0 0 3 0 0 0 3 0 0 0 3 0 3 0 3 0 3 0 3 3 0 3 0 3 0 50*3 30*0 7*3 40*0 36*3 45*0 22*3 0 0 0 3
  //   5*0 3 0 3 0 3 0 3 0 0 3 3 3 0 3 0 0 51*3 30*0 7*3 40*0 36*3 45*0 21*3 0 0 3 0 0 0 3 0 3 0 0 0 3 0 0
  //   3 0 3 3 0 3 0 3 0 3 3 0 50*3 30*0 7*3 40*0 36*3 45*0 21*3 0 0 3 0 0 0 3 0 0 0 3 0 3 0 0 3 0 3 0 3 3
  //   0 3 0 3 0 51*3 30*0 7*3 40*0 36*3 45*0 21*3 0 0 3 0 3 0 0 0 3 0 0 0 3 0 0 3 3 0 3 0 3 0 3 3 0 3 0
  //   50*3 30*0 7*3 40*0 36*3 45*0 21*3 0 0 3 0 3 5*0 3 0 3 0 0 3 3 0 0 3 3 0 3 3 0 0 51*3 30*0 7*3 41*0 3
  //   0 3 0 3 0 3 0 3 0 3 0 5*3 5*0 8*3 57*0 15*3 5*0 3 0 3 0 0 0 3 0 7 0 0 7 7 0 7 3 0 0 3 3 0 3 6*0 3
  //   6*0 3 6*0 3 6*0 3 6*0 3 6*0 3 6*0 3 36*0 3 41*0 3 0 3 0 3 0 3 0 3 0 3 0 5*3 5*0 8*3 57*0 15*3 5*0 3
  //   0 0 0 3 0 3 0 7 0 0 7 0 7 7 3 0 0 3 0 3 3 6*0 3 6*0 3 6*0 3 6*0 3 6*0 3 6*0 3 6*0 3 36*0 3 41*0 3 0
  //   3 0 3 0 3 0 3 0 3 0 5*3 5*0 8*3 57*0 15*3 0 0 0 3 0 0 0 3 0 0 0 3 0 7 0 7 0 7 0 7 3 0 3 0 3 0 3 6*0
  //   3 6*0 3 6*0 3 6*0 3 6*0 3 6*0 3 6*0 3 36*0 3 41*0 3 0 3 0 3 0 3 0 3 0 3 0 5*3 5*0 8*3 57*0 15*3 0 0
  //   0 3 5*0 3 0 3 0 7 0 7 0 0 7 7 3 0 3 0 0 3 3 6*0 3 6*0 3 6*0 3 6*0 3 6*0 3 6*0 3 6*0 3 36*0 3 41*0 3
  //   0 3 0 3 0 3 0 3 0 3 0 5*3 5*0 8*3 57*0 14*3 0 0 3 0 0 0 3 0 3 0 0 0 3 0 0 7 0 7 7 0 7 0 3 0 3 3 0 3
  //   6*0 3 6*0 3 6*0 3 6*0 3 6*0 3 6*0 3 6*0 3 36*0 3 41*0 3 0 3 0 3 0 3 0 3 0 3 0 5*3 5*0 8*3 57*0 14*3
  //   0 0 3 0 0 0 3 0 0 0 3 0 3 0 0 7 0 7 0 7 7 0 3 0 3 0 3 3 6*0 3 6*0 3 6*0 3 6*0 3 6*0 3 6*0 3 6*0 3
  //   36*0 3 41*0 3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
endmodule

module StepCounter (
  input  Clk,
  input  NotReset,
  input  Clear,
  input  NotHalt,
  input  NotWait,
  output [3:0] Step
);

  wire and_1_out, n74161_1_pin3, n74161_1_pin4, n74161_1_pin5, n74161_1_pin6, n74161_1_pin10, not_1_out;

  not not_1 (not_1_out, Clear);
  and and_1 (and_1_out, NotHalt, NotWait);
  _74161 u_74161_1 (
    .pin1(NotReset), .pin2(Clk), .pin3(n74161_1_pin3), .pin4(n74161_1_pin4), .pin5(n74161_1_pin5),
    .pin6(n74161_1_pin6), .pin7(and_1_out), .pin14(Step[0]), .pin13(Step[1]), .pin12(Step[2]),
    .pin11(Step[3]), .pin10(n74161_1_pin10), .pin9(not_1_out));  // open: pin15
  // also tied to GND on the sheet: {n74161_1_pin3, n74161_1_pin4, n74161_1_pin5, n74161_1_pin6}
  // also tied to VCC on the sheet: n74161_1_pin10
endmodule

module ProgramCounter (
  input  NotReset,
  input  HFromD,
  input  Clk,
  input  HToD,
  input  [7:0] DIn,
  input  LFromD,
  input  NotInc,
  input  LToD,
  output [7:0] DOut
);

  wire and_1_out, counter_2_carry, not_1_out, not_2_out;
  wire [3:0] counter_1_q, counter_1_q_2, counter_2_q, counter_2_q_2;

  not not_1 (not_1_out, NotReset);
  not not_2 (not_2_out, NotInc);
  Counter counter_1 (
    .clr(not_1_out), .load(HFromD), .up(not_2_out), .count(and_1_out), .clk(Clk), .D(DIn),
    .Q({counter_1_q_2, counter_1_q}));  // open: carry
  and and_1 (and_1_out, not_2_out, counter_2_carry);
  Counter counter_2 (
    .clr(not_1_out), .load(LFromD), .up(not_2_out), .count(not_2_out), .clk(Clk), .D(DIn),
    .carry(counter_2_carry), .Q({counter_2_q_2, counter_2_q}));
  assign DOut = HToD ? {counter_1_q_2, counter_1_q} : 8'bz;  // Controlled_Buffer controlled_buffer_1
  assign DOut = LToD ? {counter_2_q_2, counter_2_q} : 8'bz;  // Controlled_Buffer controlled_buffer_2
  Hex_Digit_Display hex_digit_display_1 (.value(counter_1_q_2));  // open: dp
  Hex_Digit_Display hex_digit_display_2 (.value(counter_1_q));  // open: dp
  Hex_Digit_Display hex_digit_display_3 (.value(counter_2_q_2));  // open: dp
  Hex_Digit_Display hex_digit_display_4 (.value(counter_2_q));  // open: dp
endmodule

module AddressRegister (
  input  NotReset,
  input  HFromD,
  input  Clk,
  input  [7:0] DIn,
  input  LFromD,
  input  NotInc,
  input  NotDec,
  output [15:0] Address
);

  wire and_1_out, counter_2_carry, not_1_out, not_2_out, not_3_out, or_1_out;

  not not_1 (not_1_out, NotReset);
  not not_2 (not_2_out, NotInc);
  not not_3 (not_3_out, NotDec);
  or or_1 (or_1_out, not_2_out, not_3_out);
  Counter counter_1 (
    .clr(not_1_out), .load(HFromD), .up(not_2_out), .count(and_1_out), .clk(Clk), .D(DIn), .Q(Address[15:8]));  // open: carry
  and and_1 (and_1_out, or_1_out, counter_2_carry);
  Counter counter_2 (
    .clr(not_1_out), .load(LFromD), .up(not_2_out), .count(or_1_out), .clk(Clk), .D(DIn),
    .carry(counter_2_carry), .Q(Address[7:0]));
  Hex_Digit_Display hex_digit_display_1 (.value(Address[15:12]));  // open: dp
  Hex_Digit_Display hex_digit_display_2 (.value(Address[11:8]));  // open: dp
  Hex_Digit_Display hex_digit_display_3 (.value(Address[7:4]));  // open: dp
  Hex_Digit_Display hex_digit_display_4 (.value(Address[3:0]));  // open: dp
endmodule
